# Fritzing sketch EMFduino_schematic (saved by Fritzing 0.9.10b)
circuit board: 8.46667cm x 5.64444cm
breadboards: 2

parts:
  D5 = Rectifier Diode [package="Melf DO-213 AA [SMD]"]
  D6 = Rectifier Diode [package="Melf DO-213 AA [SMD]"]
  D7 = Rectifier Diode [package="Melf DO-213 AA [SMD]"]
  D8 = Rectifier Diode [package="Melf DO-213 AA [SMD]"]
  U3 = Transformer [package=transformer]
  Power_plug2 = Power plug
  U4 = SWITCH-SPST-2 [package=switch-spst-vertical]
  Fuse2 = Fuse with Handler [part_number=Htc-15m]
  Bauteil2 = Arduino Nano (Rev3.0) (ICSP)
  Q1 = Basic FET N-Channel [package="D2Pak [SMD]"]
  R3 = Resistor [tolerance=±5% resistance=220 package="1206 [SMD]"]
  R5 = Resistor [tolerance=±5% resistance=10k package="1206 [SMD]"]
  R6 = Resistor [tolerance=±5% resistance=10k package="1206 [SMD]"]
  R7 = Resistor [tolerance=±5% resistance=10k package="1206 [SMD]"]
  ZS-042_RTC1 = ZS-042 RTC Module
  C1 = Electrolytic Capacitor [capacitance=2.2µF voltage=50V package="100 mil [THT, electrolytic]"]
  C2 = Electrolytic Capacitor [capacitance=1µF voltage=50V package="100 mil [THT, electrolytic]"]
  R8 = Resistor [tolerance=±5% power=0.25 resistance=1k package=THT]

nets:
  N1: D5.cathode, D8.cathode, R8.Pin_0
  N2: D5.anode, D7.cathode, U3.3
  N3: D6.cathode, D8.anode, U3.2
  GND: D6.anode, D7.anode, Bauteil2.GND, R5.Pin_0, R6.Pin_1, ZS-042_RTC1.GND, C2.-
  N4: U3.1, Power_plug2.GND
  N5: U3.4, Fuse2.Connector2
  N6: Power_plug2.VCC, U4.P
  N7: Bauteil2.D2, Q1.source, R5.Pin_1
  N8: Bauteil2.D3, R7.Pin_1, ZS-042_RTC1.SQW
  5V: Bauteil2.5V, R3.Pin_1, R7.Pin_0, ZS-042_RTC1.VCC
  N9: Bauteil2.A5, ZS-042_RTC1.SCL
  N10: Bauteil2.A4, ZS-042_RTC1.SDA
  N11: Q1.Gate, R6.Pin_0, C1.+, R8.Pin_1
  N12: Q1.drain, R3.Pin_0
  N13: C1.-, C2.+

notes:
  Transformer 230 Volt to 4 Volt 2A AC
  230V AC mains connection
  Bridge rectifier B40R
  Power switch and fuse
  R3
  220 Ω
  dropping resistor
  R2
  10 kΩ
  Pull-Down
  R5
  10 kΩ
  Pull-Down
  Q1
  N-Channel
  MOSFET
  IRLZ 44N
  RTC
  DS3231
  R6
  10 kΩ
  Pull-Up
  C1
  2.2 µF
  C2
  1 µF
  R1
  1 kΩ
  dropping resistor as a part of RC Lowpass
